// Digital circuit alu.dig as structural Verilog
module alu (
  input  [31:0] A,
  input  [31:0] B,
  input  [2:0] ALUOp,
  output [31:0] R,
  output [3:0] NZCV,
  output N,
  output Z,
  output C,
  output V
);

  wire and_2_out, and_3_out;
  wire [31:0] add_1_s, and_1_out, mul_1_mul, not_1_out, RSB_s, sub_1_s;
  wire [63:32] mul_1_mul_2;

  Add #(.Bits(32)) add_1 (.a(A), .b(B), .c_i(1'b0), .s(add_1_s));  // open: c_o
  Sub #(.Bits(32)) sub_1 (.a(A), .b(B), .c_i(1'b0), .s(sub_1_s));  // open: c_o
  Mul #(.Bits(32)) mul_1 (.a(A), .b(B), .mul({mul_1_mul_2, mul_1_mul}));
  Sub #(.Bits(32)) RSB (.a(B), .b(A), .c_i(1'b0), .s(RSB_s));  // open: c_o
  assign and_1_out = A & B;  // And and_1, 32 bits wide
  Comparator #(.Bits(32)) Zero (.a({N, R[30:0]}), .b({32{1'b0}}), .eq(NZCV[1]));  // open: gt, lt
  Comparator #(.Bits(32)) Carry (.a(B), .b(A), .gt(C));  // open: eq, lt
  and and_2 (and_2_out, ~A[31], B[31], N);  // And
  and and_3 (and_3_out, A[31], ~B[31], ~N);  // And
  assign not_1_out = ~B;  // Not not_1, 32 bits wide
  or or_1 (NZCV[3], and_2_out, and_3_out);
  Multiplexer #(.Selector_Bits(3), .Bits(32)) multiplexer_1 (
    .sel(ALUOp), .in_0(add_1_s), .in_1(sub_1_s), .in_2(mul_1_mul), .in_3(B), .in_4(RSB_s), .in_5(and_1_out),
    .in_6(not_1_out), .in_7({32{1'b0}}), .out({N, R[30:0]}));

  assign {NZCV[2], NZCV[0]} = {C, N};
  assign R[31] = N;
  assign V = NZCV[3];
  assign Z = NZCV[1];
endmodule
