// Digital circuit control_unit.dig as structural Verilog
module control_unit (
  input  [31:0] iw,
  input  [3:0] NZCV,
  input  CLK,
  output RFW,
  output [1:0] EXTop,
  output ALUSrcB,
  output [2:0] ALUop,
  output [1:0] PCsel,
  output [1:0] RR0sel,
  output [1:0] RR1sel,
  output [1:0] WRsel,
  output WDsel,
  output RR2sel,
  output MR,
  output MW,
  output SHen
);

  wire AL_eq, and_1_out, and_2_out, and_3_out, and_4_out, and_5_out, and_6_out, C, comparator_2_eq, condex,
       decoder_1_cpsrw, EQ_eq, GE_eq, GT_eq, LE_eq, LT_eq, N, N__eq_V, N_eq_V, NE_eq, or_1_out, V, Z;
  wire [1:0] decoder_1_pcsel;

  Register #(.Bits(4)) CPSR (.D(NZCV), .C(CLK), .en(decoder_1_cpsrw), .Q({V, C, Z, N}));
  decoder decoder_1 (
    .IW(iw), .RFW(RFW), .EXTop(EXTop), .ALUSrcB(ALUSrcB), .ALUop(ALUop), .PCsel(decoder_1_pcsel),
    .RR0sel(RR0sel), .RR1sel(RR1sel), .RR2sel(RR2sel), .WRsel(WRsel), .WDsel(WDsel), .MR(MR), .MW(MW),
    .CPSRW(decoder_1_cpsrw), .SHen(SHen));
  Comparator #(.Bits(4)) AL (.a(iw[31:28]), .b(4'b1110), .eq(AL_eq));  // open: gt, lt
  Comparator #(.Bits(4)) EQ (.a(iw[31:28]), .b(4'b0000), .eq(EQ_eq));  // open: gt, lt
  Comparator #(.Bits(4)) NE (.a(iw[31:28]), .b(4'b0001), .eq(NE_eq));  // open: gt, lt
  Comparator #(.Bits(4)) GE (.a(iw[31:28]), .b(4'b1010), .eq(GE_eq));  // open: gt, lt
  Comparator #(.Bits(4)) LT (.a(iw[31:28]), .b(4'b1011), .eq(LT_eq));  // open: gt, lt
  Comparator #(.Bits(4)) GT (.a(iw[31:28]), .b(4'b1100), .eq(GT_eq));  // open: gt, lt
  Comparator #(.Bits(4)) LE (.a(iw[31:28]), .b(4'b1101), .eq(LE_eq));  // open: gt, lt
  and and_1 (and_1_out, Z, EQ_eq);
  and and_2 (and_2_out, ~Z, NE_eq);  // And
  Comparator comparator_1 (.a(N), .b(V), .eq(N_eq_V));  // open: gt, lt
  Comparator comparator_2 (.a(N), .b(V), .eq(comparator_2_eq));  // open: gt, lt
  or or_1 (or_1_out, N__eq_V, Z);
  and and_3 (and_3_out, N_eq_V, GE_eq);
  not not_1 (N__eq_V, comparator_2_eq);
  and and_4 (and_4_out, N__eq_V, LT_eq);
  and and_5 (and_5_out, ~Z, GT_eq, N_eq_V);  // And
  and and_6 (and_6_out, or_1_out, LE_eq);
  or or_2 (condex, AL_eq, and_1_out, and_2_out, and_3_out, and_4_out, and_5_out, and_6_out);
  Multiplexer #(.Bits(2)) multiplexer_1 (.sel(condex), .in_0(2'b00), .in_1(decoder_1_pcsel), .out(PCsel));
  // Probe on RFW
  // Probe on EXTop
  // Probe on ALUSrcB
  // Probe on ALUop
  // Probe on RR0sel
  // Probe on RR1sel
  // Probe on RR2sel
  // Probe on WRsel
  // Probe on WDsel
  // Probe on MR
  // Probe on MW
  // Probe on SHen
  // Probe on PCsel
endmodule
