// Digital circuit decoder.dig as structural Verilog
module decoder (
  input  [31:0] IW,
  output RFW,
  output [1:0] EXTop,
  output ALUSrcB,
  output [2:0] ALUop,
  output [1:0] PCsel,
  output [1:0] RR0sel,
  output RR1sel,
  output [1:0] WRsel,
  output WDsel,
  output RR2sel,
  output MR,
  output MW,
  output CPSRW,
  output SHen
);

  wire add_i_eq, add_r_eq, and_1_out, and_i_eq, and_r_eq, b_eq, bl_eq, bx_eq, cmp_i_eq, cmp_r_eq,
       ldr_i__down_eq, ldr_i__up_eq, ldr_r_eq, mov_i_eq, mov_r_eq, mul_2_eq, mul_eq, mvn_i_eq, rsb_i_eq,
       rsb_r_eq, str_i__down_eq, str_i__up_eq, str_r_eq, sub_i_eq, sub_r_eq;
  wire [4:0] priorityencoder_1_num;

  Comparator #(.Bits(8)) add_r (.a(IW[27:20]), .b(8'h8), .eq(add_r_eq));  // open: gt, lt
  Comparator #(.Bits(8)) add_i (.a(IW[27:20]), .b(8'h28), .eq(add_i_eq));  // open: gt, lt
  Comparator #(.Bits(8)) mov_r (.a(IW[27:20]), .b(8'h1a), .eq(mov_r_eq));  // open: gt, lt
  Comparator #(.Bits(8)) mov_i (.a(IW[27:20]), .b(8'h3a), .eq(mov_i_eq));  // open: gt, lt
  Comparator #(.Bits(8)) sub_r (.a(IW[27:20]), .b(8'h4), .eq(sub_r_eq));  // open: gt, lt
  Comparator #(.Bits(8)) sub_i (.a(IW[27:20]), .b(8'h24), .eq(sub_i_eq));  // open: gt, lt
  Comparator #(.Bits(8)) rsb_r (.a(IW[27:20]), .b(8'h6), .eq(rsb_r_eq));  // open: gt, lt
  Comparator #(.Bits(8)) rsb_i (.a(IW[27:20]), .b(8'h26), .eq(rsb_i_eq));  // open: gt, lt
  Comparator #(.Bits(8)) and_r (.a(IW[27:20]), .b({8{1'b0}}), .eq(and_r_eq));  // open: gt, lt
  Comparator #(.Bits(8)) and_i (.a(IW[27:20]), .b(8'h20), .eq(and_i_eq));  // open: gt, lt
  Comparator #(.Bits(8)) cmp_r (.a(IW[27:20]), .b(8'h15), .eq(cmp_r_eq));  // open: gt, lt
  Comparator #(.Bits(8)) cmp_i (.a(IW[27:20]), .b(8'h35), .eq(cmp_i_eq));  // open: gt, lt
  Comparator #(.Bits(8)) mvn_i (.a(IW[27:20]), .b(8'h3e), .eq(mvn_i_eq));  // open: gt, lt
  // Probe on IW[27:20]
  // Probe on IW[27:24]
  // Probe on IW[27:4]
  // Probe on IW[27:22]
  // Probe on IW[7:4]
  Comparator #(.Bits(8)) ldr_r (.a(IW[27:20]), .b(8'h79), .eq(ldr_r_eq));  // open: gt, lt
  Comparator #(.Bits(8)) ldr_i__down (.a(IW[27:20]), .b(8'h51), .eq(ldr_i__down_eq));  // open: gt, lt
  Comparator #(.Bits(8)) ldr_i__up (.a(IW[27:20]), .b(8'h59), .eq(ldr_i__up_eq));  // open: gt, lt
  Comparator #(.Bits(8)) str_r (.a(IW[27:20]), .b(8'h78), .eq(str_r_eq));  // open: gt, lt
  Comparator #(.Bits(8)) str_i__down (.a(IW[27:20]), .b(8'h50), .eq(str_i__down_eq));  // open: gt, lt
  Comparator #(.Bits(8)) str_i__up (.a(IW[27:20]), .b(8'h58), .eq(str_i__up_eq));  // open: gt, lt
  Comparator #(.Bits(6)) mul (.a(IW[27:22]), .b({6{1'b0}}), .eq(mul_eq));  // open: gt, lt
  Comparator #(.Bits(4)) mul_2 (.a(IW[7:4]), .b(4'b1001), .eq(mul_2_eq));  // open: gt, lt
  and and_1 (and_1_out, mul_eq, mul_2_eq);
  Comparator #(.Bits(4)) b (.a(IW[27:24]), .b(4'b1010), .eq(b_eq));  // open: gt, lt
  Comparator #(.Bits(4)) bl (.a(IW[27:24]), .b(4'b1011), .eq(bl_eq));  // open: gt, lt
  Comparator #(.Bits(24)) bx (.a(IW[27:4]), .b(24'h12fff1), .eq(bx_eq));  // open: gt, lt
  PriorityEncoder #(.Selector_Bits(5)) priorityencoder_1 (
    .in0(add_r_eq), .in1(add_i_eq), .in2(mov_r_eq), .in3(mov_i_eq), .in4(sub_r_eq), .in5(sub_i_eq),
    .in6(rsb_r_eq), .in7(rsb_i_eq), .in8(and_r_eq), .in9(and_i_eq), .in10(cmp_r_eq), .in11(cmp_i_eq),
    .in12(mvn_i_eq), .in13(ldr_r_eq), .in14(ldr_i__down_eq), .in15(ldr_i__up_eq), .in16(str_r_eq),
    .in17(str_i__down_eq), .in18(str_i__up_eq), .in19(and_1_out), .in20(b_eq), .in21(bl_eq), .in22(bx_eq),
    .in23(1'b0), .in24(1'b0), .in25(1'b0), .in26(1'b0), .in27(1'b0), .in28(1'b0), .in29(1'b0), .in30(1'b0),
    .in31(1'b0), .num(priorityencoder_1_num));  // open: any
  ROM #(.AddrBits(5), .Bits(20)) rom_1 (
    .A(priorityencoder_1_num), .sel(1'b1),
    .D({RFW, EXTop, ALUSrcB, ALUop, PCsel, RR0sel, RR1sel, RR2sel, WRsel, WDsel, MR, MW, CPSRW, SHen}));
  // Probe on {RFW, EXTop, ALUSrcB, ALUop, PCsel, RR0sel, RR1sel, RR2sel, WRsel, WDsel, MR, MW, CPSRW, SHen}
  // Probe on RFW
  // Probe on EXTop
  // Probe on ALUSrcB
  // Probe on ALUop
  // Probe on PCsel
  // Probe on RR0sel
  // Probe on RR1sel
  // Probe on RR2sel
  // Probe on WRsel
  // Probe on WDsel
  // Probe on MR
  // Probe on MW
  // Probe on CPSRW
  // Probe on SHen

  // Other names for the same wires on the sheet: bits4_7[3:0] = IW[7:4]; bits4_27[23:0] = IW[27:4];
  //   bits20_27[7:0] = IW[27:20]; bits22_27[5:0] = IW[27:22]; bits24_27[3:0] = IW[27:24]

  // Notes on the sheet:
  //   contents of rom_1 (hex, n*v repeats v):
  //   80000,90000,86081,96000,82000,92000,88000,98000,8a000,9a000,2002
  //   ,12002,9c000,80089,b2008,b0008,85,32104,30104,84440,50a00,d0a30,1000
endmodule
