// Digital circuit extender.dig as structural Verilog
module extender (
  input  [31:0] iw,
  input  [1:0] EXTOp,
  output [31:0] extimm
);

  wire [31:0] Branch_Offset_out, Words_out;

  BitExtender #(.inputBits(24), .outputBits(32)) Branch_Offset (.in(iw[23:0]), .out(Branch_Offset_out));
  BarrelShifter #(.Bits(32), .direction("right")) Words (.in(Branch_Offset_out), .shift(6'b000010), .out(Words_out));
  Multiplexer #(.Selector_Bits(2), .Bits(32)) multiplexer_1 (
    .sel(EXTOp), .in_0({{24{1'b0}}, iw[7:0]}), .in_1({{20{1'b0}}, iw[11:0]}), .in_2(Words_out),
    .in_3({{27{1'b0}}, iw[11:7]}), .out(extimm));
  // Pins of 1 and 32 bits meet at extimm
endmodule
