// Digital circuit project06.dig as structural Verilog
module project06 (
  input  CLR,
  input  CLK,
  input  [4:0] PROG,
  output DONE,
  output [31:0] R0,
  output [31:0] R2
);

  wire a_mul, ALUSrcB, C, CLK_t, i_dp, MR, MW, N, RFW, RR2sel, SHen, V, WDsel, Z;
  wire [1:0] EXTop, PCsel, RR0sel, RR1sel, WRsel;
  wire [2:0] ALUop;
  wire [3:0] cond, multiplexer_2_out, multiplexer_3_out, multiplexer_4_out, multiplexer_5_out, NZCV;
  wire [6:0] PC_q_2;
  wire [23:0] b_offset;
  wire [27:24] iw;
  wire [31:0] add_1_s, add_2_s, alu_1_r, extender_1_p3, multiplexer_1_out, multiplexer_6_out,
       multiplexer_7_out, multiplexer_8_out, PC_q, r1, r3, r4, r5, r6, r7, r8, r9, r10, r11, r12, r13, r14,
       r15, ramdualport_1_d, reg_file_1_rd0, reg_file_1_rd1, reg_file_1_rd2, shifter_1_r;

  control_unit control_unit_1 (
    .iw({cond, iw[27:26], i_dp, iw[24], b_offset[23:22], a_mul, b_offset[20:0]}), .NZCV(NZCV), .CLK(CLK_t),
    .RFW(RFW), .EXTop(EXTop), .ALUSrcB(ALUSrcB), .ALUop(ALUop), .PCsel(PCsel), .RR0sel(RR0sel),
    .RR1sel(RR1sel), .RR2sel(RR2sel), .WRsel(WRsel), .WDsel(WDsel), .MR(MR), .MW(MW), .SHen(SHen));
  and and_1 (CLK_t, CLK, ~DONE);  // And
  _32_bit_reg PC (.D(multiplexer_1_out), .CLK(CLK_t), .CLR(CLR), .EN(1'b1), .Q({PC_q[31:9], PC_q_2, PC_q[1:0]}));
  // Probe on {cond, iw[27:26], i_dp, iw[24], b_offset[23:22], a_mul, b_offset[20:0]}
  Multiplexer #(.Selector_Bits(2), .Bits(32)) multiplexer_1 (
    .sel(PCsel), .in_0(add_1_s), .in_1(multiplexer_8_out), .in_2(reg_file_1_rd1), .in_3({32{1'b0}}),
    .out(multiplexer_1_out));
  // instruction_memory instruction_memory_1: pin names not known; wires that end beside it: PC_q_2, PROG, {cond, iw[27:26], i_dp, iw[24], b_offset[23:22], a_mul, b_offset[20:0]}
  Add #(.Bits(32)) add_1 (.a({PC_q[31:9], PC_q_2, PC_q[1:0]}), .b(32'h4), .c_i(1'b0), .s(add_1_s));  // open: c_o
  Add #(.Bits(32)) add_2 (.a(add_1_s), .b(32'h4), .c_i(1'b0), .s(add_2_s));  // open: c_o
  // Probe on R0
  // Probe on r1
  // Probe on R2
  // Probe on r3
  // Probe on cond
  // Probe on cond
  // Probe on cond
  // Probe on cond
  // Probe on r4
  // Probe on r5
  // Probe on r6
  // Probe on r7
  // Probe on iw[27:26]
  // Probe on {iw[27:26], i_dp, iw[24], b_offset[23]}
  // Probe on iw[27:26]
  // Probe on {iw[27:26], i_dp}
  Multiplexer #(.Selector_Bits(2), .Bits(4)) multiplexer_2 (
    .sel(RR0sel), .in_0(b_offset[19:16]), .in_1(4'b1111), .in_2(b_offset[11:8]), .in_3(b_offset[15:12]),
    .out(multiplexer_2_out));
  Multiplexer #(.Selector_Bits(2), .Bits(4)) multiplexer_3 (
    .sel(RR1sel), .in_0(b_offset[3:0]), .in_1(b_offset[19:16]), .in_2(b_offset[15:12]), .in_3(4'b0000),
    .out(multiplexer_3_out));
  Multiplexer #(.Bits(4)) multiplexer_4 (.sel(RR2sel), .in_0(4'b0000), .in_1(b_offset[11:8]), .out(multiplexer_4_out));
  Multiplexer #(.Selector_Bits(2), .Bits(4)) multiplexer_5 (
    .sel(WRsel), .in_0(b_offset[15:12]), .in_1(4'b1110), .in_2(b_offset[19:16]), .in_3(4'b0000),
    .out(multiplexer_5_out));
  Multiplexer #(.Bits(32)) multiplexer_6 (
    .sel(WDsel), .in_0(multiplexer_8_out), .in_1(add_1_s), .out(multiplexer_6_out));
  // Probe on i_dp
  // Probe on a_mul
  // Probe on i_dp
  // Probe on iw[24]
  // Probe on {iw[24], b_offset[23:22], a_mul}
  // Probe on b_offset[20]
  // Probe on iw[24]
  reg_file reg_file_1 (
    .ReadReg0(multiplexer_2_out), .ReadReg1(multiplexer_3_out), .ReadReg2(multiplexer_4_out),
    .WriteReg(multiplexer_5_out), .WriteData(multiplexer_6_out), .WriteEn(RFW), .PC(add_2_s), .CLK(CLK_t),
    .CLR(CLR), .RD0(reg_file_1_rd0), .RD1(reg_file_1_rd1), .RD2(reg_file_1_rd2), .r0(R0), .r1(r1), .r2(R2),
    .r3(r3), .r4(r4), .r5(r5), .r6(r6), .r7(r7), .r8(r8), .r9(r9), .r10(r10), .r11(r11), .r12(r12),
    .r13(r13), .r14(r14), .r15(r15));
  // Probe on r8
  // Probe on r9
  // Probe on r10
  // Probe on r11
  // Probe on b_offset[23]
  // Probe on {b_offset[23:22], a_mul, b_offset[20:0]}
  // Probe on b_offset[20]
  // Probe on b_offset[19:16]
  // Probe on b_offset[22]
  // Probe on r12
  // Probe on r13
  // Probe on r14
  // Probe on r15
  // Probe on b_offset[19:16]
  // Probe on b_offset[15:12]
  // Probe on a_mul
  // Probe on b_offset[15:12]
  // Probe on b_offset[11:8]
  // Probe on b_offset[20]
  // Probe on N
  // Probe on Z
  // Probe on C
  // Probe on V
  // Probe on b_offset[3:0]
  // Probe on b_offset[7:0]
  // Probe on b_offset[19:16]
  // Probe on b_offset[7:4]
  // Probe on b_offset[15:12]
  shifter shifter_1 (
    .D(reg_file_1_rd0), .iw({cond, iw[27:26], i_dp, iw[24], b_offset[23:22], a_mul, b_offset[20:0]}),
    .Rs(reg_file_1_rd2), .Shen(SHen), .R(shifter_1_r));
  // Probe on b_offset[3:0]
  // Probe on b_offset[3:0]
  // Probe on b_offset[11:0]
  Multiplexer #(.Bits(32)) multiplexer_7 (
    .sel(ALUSrcB), .in_0(shifter_1_r), .in_1(extender_1_p3), .out(multiplexer_7_out));
  // extender extender_1: pin names not known; wires that end beside it: {cond, iw[27:26], i_dp, iw[24], b_offset[23:22], a_mul, b_offset[20:0]}, EXTop, extender_1_p3
  Comparator #(.Bits(32)) comparator_1 (
    .a({cond, iw[27:26], i_dp, iw[24], b_offset[23:22], a_mul, b_offset[20:0]}), .b(32'he2800000), .eq(DONE));  // open: gt, lt
  Multiplexer #(.Bits(32)) multiplexer_8 (.sel(MR), .in_0(alu_1_r), .in_1(ramdualport_1_d), .out(multiplexer_8_out));
  // Probe on extender_1_p3
  alu alu_1 (
    .A(reg_file_1_rd0), .B(multiplexer_7_out), .ALUOp(ALUop), .R(alu_1_r), .NZCV(NZCV), .N(N), .Z(Z), .C(C),
    .V(V));
  RAMDualPort #(.AddrBits(10), .Bits(32)) ramdualport_1 (
    .A({2'b00, alu_1_r[9:2]}), .Din(reg_file_1_rd1), .str(MR), .C(CLK_t), .ld(MW), .D(ramdualport_1_d));

  // Other names for the same wires on the sheet: imm[7:0] = b_offset[7:0]; immoff[11:0] = b_offset[11:0];
  //   iw (some bits) = {cond, i_dp, b_offset[23:22], a_mul, b_offset[20:0]}; rm[3:0] = b_offset[3:0];
  //   rm_mul[3:0] = b_offset[3:0]; opmul4[3:0] = b_offset[7:4]; rs_mul[3:0] = b_offset[11:8];
  //   rd[3:0] = b_offset[15:12]; rn_mul[3:0] = b_offset[15:12]; rd_mul[3:0] = b_offset[19:16];
  //   rn[3:0] = b_offset[19:16]; l_sdt = b_offset[20]; s_dp = b_offset[20]; s_mul = b_offset[20];
  //   b_offset[21] = a_mul; opc[3:0] = {iw[24], b_offset[23:22], a_mul}; w_sdt = a_mul; b_sdt = b_offset[22];
  //   opmul6[4:0] = {iw[27:26], i_dp, iw[24], b_offset[23]}; u_sdt = b_offset[23]; lb = iw[24]; p_sdt = iw[24];
  //   i_sdt = i_dp; opb3[2:0] = {iw[27:26], i_dp}; op2[1:0] = iw[27:26]; opmul2[1:0] = iw[27:26]

  // Notes on the sheet:
  //   DP
  //   MUL
  //   SDT
  //   B
  //   SP
  //   LR
  //   PC
endmodule
