// Digital circuit reg_file.dig as structural Verilog
module reg_file (
  input  [3:0] ReadReg0,
  input  [3:0] ReadReg1,
  input  [3:0] WriteReg,
  input  WriteEn,
  input  [31:0] WriteData,
  input  CLR,
  input  [31:0] PC,
  input  CLK,
  input  [3:0] ReadReg2,
  output [31:0] RD0,
  output [31:0] RD1,
  output [31:0] r0,
  output [31:0] r1,
  output [31:0] r2,
  output [31:0] r3,
  output [31:0] r4,
  output [31:0] r5,
  output [31:0] r6,
  output [31:0] r7,
  output [31:0] r8,
  output [31:0] r9,
  output [31:0] r10,
  output [31:0] r11,
  output [31:0] r12,
  output [31:0] r13,
  output [31:0] r14,
  output [31:0] r15,
  output [31:0] RD2
);

  wire and_1_out, and_2_out, and_3_out, and_4_out, and_5_out, and_6_out, and_7_out, and_8_out, and_9_out,
       and_10_out, and_11_out, and_12_out, and_13_out, and_14_out, and_15_out, decoder_1_out_0,
       decoder_1_out_1, decoder_1_out_2, decoder_1_out_3, decoder_1_out_4, decoder_1_out_5, decoder_1_out_6,
       decoder_1_out_7, decoder_1_out_8, decoder_1_out_9, decoder_1_out_10, decoder_1_out_11,
       decoder_1_out_12, decoder_1_out_13, decoder_1_out_14;

  Decoder #(.Selector_Bits(4)) decoder_1 (
    .sel(WriteReg), .out_0(decoder_1_out_0), .out_1(decoder_1_out_1), .out_2(decoder_1_out_2),
    .out_3(decoder_1_out_3), .out_4(decoder_1_out_4), .out_5(decoder_1_out_5), .out_6(decoder_1_out_6),
    .out_7(decoder_1_out_7), .out_8(decoder_1_out_8), .out_9(decoder_1_out_9), .out_10(decoder_1_out_10),
    .out_11(decoder_1_out_11), .out_12(decoder_1_out_12), .out_13(decoder_1_out_13), .out_14(decoder_1_out_14));  // open: out_15
  and and_1 (and_1_out, decoder_1_out_0, WriteEn);
  and and_2 (and_2_out, decoder_1_out_1, WriteEn);
  and and_3 (and_3_out, decoder_1_out_2, WriteEn);
  and and_4 (and_4_out, decoder_1_out_3, WriteEn);
  and and_5 (and_5_out, decoder_1_out_4, WriteEn);
  and and_6 (and_6_out, decoder_1_out_5, WriteEn);
  and and_7 (and_7_out, decoder_1_out_6, WriteEn);
  and and_8 (and_8_out, decoder_1_out_7, WriteEn);
  and and_9 (and_9_out, decoder_1_out_8, WriteEn);
  and and_10 (and_10_out, decoder_1_out_9, WriteEn);
  and and_11 (and_11_out, decoder_1_out_10, WriteEn);
  and and_12 (and_12_out, decoder_1_out_11, WriteEn);
  and and_13 (and_13_out, decoder_1_out_12, WriteEn);
  and and_14 (and_14_out, decoder_1_out_13, WriteEn);
  and and_15 (and_15_out, decoder_1_out_14, WriteEn);
  _32_bit_reg _32_bit_reg_1 (.D(WriteData), .CLK(CLK), .CLR(CLR), .EN(and_1_out), .Q(r0));
  _32_bit_reg _32_bit_reg_2 (.D(WriteData), .CLK(CLK), .CLR(CLR), .EN(and_2_out), .Q(r1));
  _32_bit_reg _32_bit_reg_3 (.D(WriteData), .CLK(CLK), .CLR(CLR), .EN(and_3_out), .Q(r2));
  _32_bit_reg _32_bit_reg_4 (.D(WriteData), .CLK(CLK), .CLR(CLR), .EN(and_4_out), .Q(r3));
  _32_bit_reg _32_bit_reg_5 (.D(WriteData), .CLK(CLK), .CLR(CLR), .EN(and_5_out), .Q(r4));
  _32_bit_reg _32_bit_reg_6 (.D(WriteData), .CLK(CLK), .CLR(CLR), .EN(and_6_out), .Q(r5));
  _32_bit_reg _32_bit_reg_7 (.D(WriteData), .CLK(CLK), .CLR(CLR), .EN(and_7_out), .Q(r6));
  _32_bit_reg _32_bit_reg_8 (.D(WriteData), .CLK(CLK), .CLR(CLR), .EN(and_8_out), .Q(r7));
  _32_bit_reg _32_bit_reg_9 (.D(WriteData), .CLK(CLK), .CLR(CLR), .EN(and_9_out), .Q(r8));
  _32_bit_reg _32_bit_reg_10 (.D(WriteData), .CLK(CLK), .CLR(CLR), .EN(and_10_out), .Q(r9));
  _32_bit_reg _32_bit_reg_11 (.D(WriteData), .CLK(CLK), .CLR(CLR), .EN(and_11_out), .Q(r10));
  _32_bit_reg _32_bit_reg_12 (.D(WriteData), .CLK(CLK), .CLR(CLR), .EN(and_12_out), .Q(r11));
  _32_bit_reg _32_bit_reg_13 (.D(WriteData), .CLK(CLK), .CLR(CLR), .EN(and_13_out), .Q(r12));
  _32_bit_reg _32_bit_reg_14 (.D(WriteData), .CLK(CLK), .CLR(CLR), .EN(and_14_out), .Q(r13));
  _32_bit_reg _32_bit_reg_15 (.D(WriteData), .CLK(CLK), .CLR(CLR), .EN(and_15_out), .Q(r14));
  Multiplexer #(.Selector_Bits(4), .Bits(32)) multiplexer_1 (
    .sel(ReadReg0), .in_0(r0), .in_1(r1), .in_2(r2), .in_3(r3), .in_4(r4), .in_5(r5), .in_6(r6), .in_7(r7),
    .in_8(r8), .in_9(r9), .in_10(r10), .in_11(r11), .in_12(r12), .in_13(r13), .in_14(r14), .in_15(PC),
    .out(RD0));
  Multiplexer #(.Selector_Bits(4), .Bits(32)) multiplexer_2 (
    .sel(ReadReg1), .in_0(r0), .in_1(r1), .in_2(r2), .in_3(r3), .in_4(r4), .in_5(r5), .in_6(r6), .in_7(r7),
    .in_8(r8), .in_9(r9), .in_10(r10), .in_11(r11), .in_12(r12), .in_13(r13), .in_14(r14), .in_15(PC),
    .out(RD1));
  Multiplexer #(.Selector_Bits(4), .Bits(32)) multiplexer_3 (
    .sel(ReadReg2), .in_0(r0), .in_1(r1), .in_2(r2), .in_3(r3), .in_4(r4), .in_5(r5), .in_6(r6), .in_7(r7),
    .in_8(r8), .in_9(r9), .in_10(r10), .in_11(r11), .in_12(r12), .in_13(r13), .in_14(r14), .in_15(PC),
    .out(RD2));

  assign r15 = PC;
endmodule
