// Digital circuit shifter.dig as structural Verilog
module shifter (
  input  [31:0] D,
  input  [31:0] iw,
  input  [31:0] Rs,
  input  Shen,
  output [31:0] R
);

  wire [5:0] multiplexer_1_out;
  wire [31:0] ASR_out, LSL_out, LSR_out, multiplexer_2_out;

  Multiplexer #(.Bits(6)) multiplexer_1 (.sel(iw[4]), .in_0({1'b0, iw[11:7]}), .in_1(Rs[5:0]), .out(multiplexer_1_out));
  BarrelShifter #(.Bits(32)) LSL (.in(D), .shift(multiplexer_1_out), .out(LSL_out));
  BarrelShifter #(.Bits(32), .direction("right")) LSR (.in(D), .shift(multiplexer_1_out), .out(LSR_out));
  BarrelShifter #(.Bits(32), .barrelShifterMode("arithmetic"), .direction("right")) ASR (
    .in(D), .shift(multiplexer_1_out), .out(ASR_out));
  Multiplexer #(.Selector_Bits(2), .Bits(32)) multiplexer_2 (
    .sel(iw[6:5]), .in_0(LSL_out), .in_1(LSR_out), .in_2(ASR_out), .in_3({32{1'b0}}), .out(multiplexer_2_out));
  Multiplexer #(.Bits(32)) multiplexer_3 (.sel(Shen), .in_0(D), .in_1(multiplexer_2_out), .out(R));

  // Other names for the same wires on the sheet: ShType[1:0] = iw[6:5]
endmodule
